# Fritzing sketch TicTacToeMachine (saved by Fritzing 0.8.5b)
circuit board: 10cm x 16cm
breadboards: 5

parts:
  R_in_3 = Resistor [tolerance=±5% resistance=10k package=THT]
  R_in_2 = Resistor [tolerance=±5% resistance=10k package=THT]
  R_in_1 = Resistor [tolerance=±5% resistance=10k package=THT]
  VCC1 = 4 x AAA Battery Mount
  R1R = Resistor [tolerance=±5% resistance=100 package=THT]
  R2R = Resistor [tolerance=±5% resistance=100 package=THT]
  R3R = Resistor [tolerance=±5% resistance=100 package=THT]
  LED4_R = LED - 5mm [color="Red (633nm)" package="5 mm [THT]"]
  LED5_R = LED - 5mm [color="Red (633nm)" package="5 mm [THT]"]
  LED6_R = LED - 5mm [color="Red (633nm)" package="5 mm [THT]"]
  LED7_R = LED - 5mm [color="Red (633nm)" package="5 mm [THT]"]
  LED8_R = LED - 5mm [color="Red (633nm)" package="5 mm [THT]"]
  LED9_R = LED - 5mm [color="Red (633nm)" package="5 mm [THT]"]
  R6R = Resistor [tolerance=±5% resistance=100 package=THT]
  R5R = Resistor [tolerance=±5% resistance=100 package=THT]
  R4R = Resistor [tolerance=±5% resistance=100 package=THT]
  R9R = Resistor [tolerance=±5% resistance=100 package=THT]
  R7R = Resistor [tolerance=±5% resistance=100 package=THT]
  R8R = Resistor [tolerance=±5% resistance=100 package=THT]
  Led_HR2_R = LED - 5mm [color="Infrared (940nm)" package="5 mm [THT]"]
  Led_HR3_R = LED - 5mm [color="Infrared (940nm)" package="5 mm [THT]"]
  R_HR3_R = Resistor [tolerance=±5% resistance=100 package=THT]
  J1 = male pin header, 4 pins [form="♂ (male)"]
  J2 = male pin header, 4 pins [form="♂ (male)"]
  J3 = male pin header, 4 pins [form="♂ (male)"]
  J4 = male pin header, 4 pins [form="♂ (male)"]
  J5 = male pin header, 4 pins [form="♂ (male)"]
  J6 = male pin header, 4 pins [form="♂ (male)"]
  J7 = male pin header, 4 pins [form="♂ (male)"]
  J8 = male pin header, 4 pins [form="♂ (male)"]
  J9 = male pin header, 4 pins [form="♂ (male)"]
  LED1_R = LED - 5mm [color="Red (633nm)" package="5 mm [THT]"]
  LED2_R = LED - 5mm [color="Red (633nm)" package="5 mm [THT]"]
  LED3_R = LED - 5mm [color="Red (633nm)" package="5 mm [THT]"]
  R_HR1_R1 = Resistor [tolerance=±5% resistance=100 package=THT]
  Led_HR1_R1 = LED - 5mm [color="Infrared (940nm)" package="5 mm [THT]"]
  LED7_G = LED - 5mm [color="Green (555nm)" package="5 mm [THT]"]
  LED4_G = LED - 5mm [color="Green (555nm)" package="5 mm [THT]"]
  LED1_G = LED - 5mm [color="Green (555nm)" package="5 mm [THT]"]
  LED8_G = LED - 5mm [color="Green (555nm)" package="5 mm [THT]"]
  LED5_G = LED - 5mm [color="Green (555nm)" package="5 mm [THT]"]
  LED2_G = LED - 5mm [color="Green (555nm)" package="5 mm [THT]"]
  LED9_G = LED - 5mm [color="Green (555nm)" package="5 mm [THT]"]
  LED6_G = LED - 5mm [color="Green (555nm)" package="5 mm [THT]"]
  LED3_G = LED - 5mm [color="Green (555nm)" package="5 mm [THT]"]
  R8_G = Resistor [tolerance=±5% resistance=100 package=THT]
  R9_G = Resistor [tolerance=±5% resistance=100 package=THT]
  R6_G = Resistor [tolerance=±5% resistance=100 package=THT]
  R3_G = Resistor [tolerance=±5% resistance=100 package=THT]
  R5_G = Resistor [tolerance=±5% resistance=100 package=THT]
  R2_G = Resistor [tolerance=±5% resistance=100 package=THT]
  R7_G = Resistor [tolerance=±5% resistance=100 package=THT]
  R4_G = Resistor [tolerance=±5% resistance=100 package=THT]
  R1_G = Resistor [tolerance=±5% resistance=100 package=THT]
  Led_Win_R = LED - 5mm [color="Red (633nm)" package="5 mm [THT]"]
  CMOS_AND2 = mystery part, 14 pins [chip_label="CMOS4073 (3AND)"]
  R_in_4 = Resistor [tolerance=±5% resistance=10k package=THT]
  R_in_5 = Resistor [tolerance=±5% resistance=10k package=THT]
  R_in_6 = Resistor [tolerance=±5% resistance=10k package=THT]
  R_in_7 = Resistor [tolerance=±5% resistance=10k package=THT]
  R_in_8 = Resistor [tolerance=±5% resistance=10k package=THT]
  R_in_9 = Resistor [tolerance=±5% resistance=10k package=THT]
  R_HR2_R1 = Resistor [tolerance=±5% resistance=100 package=THT]
  Led_HR3_R1 = LED - 5mm [color="Infrared (940nm)" package="5 mm [THT]"]
  Led_HR2_R1 = LED - 5mm [color="Infrared (940nm)" package="5 mm [THT]"]
  Led_HR1_R2 = LED - 5mm [color="Infrared (940nm)" package="5 mm [THT]"]
  CMOS_AND3 = mystery part, 14 pins [chip_label="CMOS4073 (3AND)"]
  R_in_10 = Resistor [tolerance=±5% resistance=10k package=THT]
  R_in_11 = Resistor [tolerance=±5% resistance=10k package=THT]
  R_in_12 = Resistor [tolerance=±5% resistance=10k package=THT]
  R_in_13 = Resistor [tolerance=±5% resistance=10k package=THT]
  R_in_14 = Resistor [tolerance=±5% resistance=10k package=THT]
  R_in_15 = Resistor [tolerance=±5% resistance=10k package=THT]
  R_in_16 = Resistor [tolerance=±5% resistance=10k package=THT]
  R_in_17 = Resistor [tolerance=±5% resistance=10k package=THT]
  R_in_18 = Resistor [tolerance=±5% resistance=10k package=THT]
  R_HR3_R1 = Resistor [tolerance=±5% resistance=100 package=THT]
  R_HR1_R2 = Resistor [tolerance=±5% resistance=100 package=THT]
  R_HR2_R2 = Resistor [tolerance=±5% resistance=100 package=THT]
  Led_HR2_R2 = LED - 5mm [color="Infrared (940nm)" package="5 mm [THT]"]
  Led_HR1_R3 = LED - 5mm [color="Infrared (940nm)" package="5 mm [THT]"]
  CMOS_AND4 = mystery part, 14 pins [chip_label="CMOS4073 (3AND)"]
  R_in_19 = Resistor [tolerance=±5% resistance=10k package=THT]
  R_in_20 = Resistor [tolerance=±5% resistance=10k package=THT]
  R_in_21 = Resistor [tolerance=±5% resistance=10k package=THT]
  R_in_22 = Resistor [tolerance=±5% resistance=10k package=THT]
  R_in_23 = Resistor [tolerance=±5% resistance=10k package=THT]
  R_in_24 = Resistor [tolerance=±5% resistance=10k package=THT]
  R_in_25 = Resistor [tolerance=±5% resistance=10k package=THT]
  R_in_26 = Resistor [tolerance=±5% resistance=10k package=THT]
  R_in_27 = Resistor [tolerance=±5% resistance=10k package=THT]
  R_HR1_R3 = Resistor [tolerance=±5% resistance=100 package=THT]
  R_HR2_R3 = Resistor [tolerance=±5% resistance=100 package=THT]
  R_in_28 = Resistor [tolerance=±5% resistance=10k package=THT]
  Led_HR3_R2 = LED - 5mm [color="Infrared (940nm)" package="5 mm [THT]"]
  Led_HR3_R3 = LED - 5mm [color="Infrared (940nm)" package="5 mm [THT]"]
  Led_HR2_R3 = LED - 5mm [color="Infrared (940nm)" package="5 mm [THT]"]
  Led_HR2_R4 = LED - 5mm [color="Infrared (940nm)" package="5 mm [THT]"]
  Led_HR2_R5 = LED - 5mm [color="Infrared (940nm)" package="5 mm [THT]"]
  Led_HR1_R4 = LED - 5mm [color="Infrared (940nm)" package="5 mm [THT]"]
  Led_HR1_R5 = LED - 5mm [color="Infrared (940nm)" package="5 mm [THT]"]
  Led_HR1_R6 = LED - 5mm [color="Infrared (940nm)" package="5 mm [THT]"]
  CMOS_AND5 = mystery part, 14 pins [chip_label="CMOS4073 (3AND)"]
  CMOS_AND6 = mystery part, 14 pins [chip_label="CMOS4073 (3AND)"]
  CMOS_AND7 = mystery part, 14 pins [chip_label="CMOS4073 (3AND)"]
  R_in_29 = Resistor [tolerance=±5% resistance=10k package=THT]
  R_in_30 = Resistor [tolerance=±5% resistance=10k package=THT]
  R_in_31 = Resistor [tolerance=±5% resistance=10k package=THT]
  R_in_32 = Resistor [tolerance=±5% resistance=10k package=THT]
  R_in_33 = Resistor [tolerance=±5% resistance=10k package=THT]
  R_in_34 = Resistor [tolerance=±5% resistance=10k package=THT]
  R_in_35 = Resistor [tolerance=±5% resistance=10k package=THT]
  R_in_36 = Resistor [tolerance=±5% resistance=10k package=THT]
  R_in_37 = Resistor [tolerance=±5% resistance=10k package=THT]
  R_in_38 = Resistor [tolerance=±5% resistance=10k package=THT]
  R_in_39 = Resistor [tolerance=±5% resistance=10k package=THT]
  R_in_40 = Resistor [tolerance=±5% resistance=10k package=THT]
  R_in_41 = Resistor [tolerance=±5% resistance=10k package=THT]
  R_in_42 = Resistor [tolerance=±5% resistance=10k package=THT]
  R_in_43 = Resistor [tolerance=±5% resistance=10k package=THT]
  R_in_44 = Resistor [tolerance=±5% resistance=10k package=THT]
  R_in_45 = Resistor [tolerance=±5% resistance=10k package=THT]
  R_in_46 = Resistor [tolerance=±5% resistance=10k package=THT]
  R_in_47 = Resistor [tolerance=±5% resistance=10k package=THT]
  R_in_48 = Resistor [tolerance=±5% resistance=10k package=THT]
  R_in_49 = Resistor [tolerance=±5% resistance=10k package=THT]
  R_in_50 = Resistor [tolerance=±5% resistance=10k package=THT]
  R_in_51 = Resistor [tolerance=±5% resistance=10k package=THT]
  R_in_52 = Resistor [tolerance=±5% resistance=10k package=THT]
  R_in_53 = Resistor [tolerance=±5% resistance=10k package=THT]
  R_in_54 = Resistor [tolerance=±5% resistance=10k package=THT]
  R_in_55 = Resistor [tolerance=±5% resistance=10k package=THT]
  R_in_56 = Resistor [tolerance=±5% resistance=10k package=THT]
  R_HR3_R2 = Resistor [tolerance=±5% resistance=100 package=THT]
  R_HR3_R3 = Resistor [tolerance=±5% resistance=100 package=THT]
  R_HR1_R4 = Resistor [tolerance=±5% resistance=100 package=THT]
  R_HR1_R5 = Resistor [tolerance=±5% resistance=100 package=THT]
  R_HR1_R6 = Resistor [tolerance=±5% resistance=100 package=THT]
  R_HR2_R4 = Resistor [tolerance=±5% resistance=100 package=THT]
  R_HR2_R5 = Resistor [tolerance=±5% resistance=100 package=THT]
  R_HR2_R6 = Resistor [tolerance=±5% resistance=100 package=THT]
  CMOS_OR2 = mystery part, 14 pins [chip_label=4OR]
  R_WIN_R1 = Resistor [tolerance=±5% resistance=100 package=THT]
  CMOS_OR3 = mystery part, 14 pins [chip_label=4OR]  # not connected
  CMOS_OR4 = mystery part, 14 pins [chip_label=4OR]  # not connected

nets:
  N1: R_in_3.Pin_0, R_in_2.Pin_0, R_in_1.Pin_0, VCC1.-, R1R.Pin_1, R2R.Pin_1, R3R.Pin_1, R6R.Pin_1, R5R.Pin_1, R4R.Pin_1, R9R.Pin_1, R7R.Pin_1, R8R.Pin_1, R_HR3_R.Pin_1, R_HR1_R1.Pin_1, R8_G.Pin_1, R9_G.Pin_1, R6_G.Pin_1, R3_G.Pin_1, R5_G.Pin_1, R2_G.Pin_1, R7_G.Pin_1, R4_G.Pin_1, R1_G.Pin_1, CMOS_AND2.pin7, R_in_4.Pin_0, R_in_5.Pin_0, R_in_6.Pin_1, R_in_7.Pin_1, R_in_8.Pin_1, R_in_9.Pin_1, R_HR2_R1.Pin_1, CMOS_AND3.pin7, R_in_10.Pin_0, R_in_11.Pin_0, R_in_12.Pin_0, R_in_13.Pin_0, R_in_14.Pin_0, R_in_15.Pin_1, R_in_16.Pin_1, R_in_17.Pin_1, R_in_18.Pin_1, R_HR3_R1.Pin_1, R_HR1_R2.Pin_1, R_HR2_R2.Pin_1, CMOS_AND4.pin7, R_in_19.Pin_0, R_in_20.Pin_0, R_in_21.Pin_0, R_in_22.Pin_0, R_in_23.Pin_0, R_in_24.Pin_1, R_in_25.Pin_1, R_in_26.Pin_1, R_in_27.Pin_1, R_HR1_R3.Pin_1, R_HR2_R3.Pin_1, R_in_28.Pin_1, CMOS_AND5.pin7, CMOS_AND6.pin7, CMOS_AND7.pin7, R_in_29.Pin_0, R_in_30.Pin_0, R_in_31.Pin_0, R_in_32.Pin_0, R_in_33.Pin_0, R_in_34.Pin_0, R_in_35.Pin_0, R_in_36.Pin_0, R_in_37.Pin_0, R_in_38.Pin_1, R_in_39.Pin_1, R_in_40.Pin_1, R_in_41.Pin_1, R_in_42.Pin_0, R_in_43.Pin_1, R_in_44.Pin_1, R_in_45.Pin_1, R_in_46.Pin_0, R_in_47.Pin_0, R_in_48.Pin_1, R_in_49.Pin_1, R_in_50.Pin_0, R_in_51.Pin_1, R_in_52.Pin_1, R_in_53.Pin_1, R_in_54.Pin_0, R_in_55.Pin_0, R_in_56.Pin_1, R_HR3_R2.Pin_1, R_HR3_R3.Pin_1, R_HR1_R4.Pin_1, R_HR1_R5.Pin_1, R_HR1_R6.Pin_1, R_HR2_R4.Pin_1, R_HR2_R5.Pin_1, R_HR2_R6.Pin_1
  N2: R_in_3.Pin_1, CMOS_AND2.pin3
  N3: R_in_2.Pin_1, CMOS_AND2.pin2
  N4: R_in_1.Pin_1, J1.pin1, LED1_R.anode, CMOS_AND2.pin1
  N5: VCC1.+, J1.pin4, J2.pin4, J3.pin4, J4.pin4, J5.pin4, J6.pin4, J7.pin4, J8.pin4, J9.pin4, CMOS_AND2.pin14, CMOS_AND3.pin14, CMOS_AND4.pin14, CMOS_AND5.pin14, CMOS_AND6.pin14, CMOS_AND7.pin14, CMOS_OR2.pin14
  N6: R1R.Pin_0, LED1_R.cathode
  N7: R2R.Pin_0, LED2_R.cathode
  N8: R3R.Pin_0, LED3_R.cathode
  N9: LED4_R.cathode, R4R.Pin_0
  N10: LED4_R.anode, J4.pin1
  N11: LED5_R.cathode, R5R.Pin_0
  N12: LED5_R.anode, J5.pin1
  N13: LED6_R.cathode, R6R.Pin_0
  N14: LED6_R.anode, J6.pin1
  N15: LED7_R.cathode, R7R.Pin_0
  N16: LED7_R.anode, J7.pin1
  N17: LED8_R.cathode, R8R.Pin_0
  N18: LED8_R.anode, J8.pin1
  N19: LED9_R.cathode, R9R.Pin_0
  N20: LED9_R.anode, J9.pin1
  N21: Led_HR2_R.cathode, R_HR2_R1.Pin_0
  N22: Led_HR2_R.anode, CMOS_AND2.pin6
  N23: Led_HR3_R.cathode, R_HR3_R.Pin_0
  N24: Led_HR3_R.anode, CMOS_AND2.pin10
  N25: J1.pin3, LED1_G.anode
  N26: J2.pin1, LED2_R.anode
  N27: J2.pin3, LED2_G.anode
  N28: J3.pin1, LED3_R.anode
  N29: J3.pin3, LED3_G.anode
  N30: J4.pin3, LED4_G.anode
  N31: J5.pin3, LED5_G.anode
  N32: J6.pin3, LED6_G.anode
  N33: J7.pin3, LED7_G.anode
  N34: J8.pin3, LED8_G.anode
  N35: J9.pin3, LED9_G.anode
  N36: R_HR1_R1.Pin_0, Led_HR1_R1.cathode
  N37: Led_HR1_R1.anode, CMOS_AND2.pin9
  N38: LED7_G.cathode, R7_G.Pin_0
  N39: LED4_G.cathode, R4_G.Pin_0
  N40: LED1_G.cathode, R1_G.Pin_0
  N41: LED8_G.cathode, R8_G.Pin_0
  N42: LED5_G.cathode, R5_G.Pin_0
  N43: LED2_G.cathode, R2_G.Pin_0
  N44: LED9_G.cathode, R9_G.Pin_0
  N45: LED6_G.cathode, R6_G.Pin_0
  N46: LED3_G.cathode, R3_G.Pin_0
  N47: Led_Win_R.cathode, R_WIN_R1.Pin_0
  N48: CMOS_AND2.pin4, R_in_4.Pin_1
  N49: CMOS_AND2.pin5, R_in_5.Pin_1
  N50: CMOS_AND2.pin8, R_in_9.Pin_0
  N51: CMOS_AND2.pin11, R_in_8.Pin_0
  N52: CMOS_AND2.pin12, R_in_7.Pin_0
  N53: CMOS_AND2.pin13, R_in_6.Pin_0
  N54: Led_HR3_R1.cathode, R_HR3_R1.Pin_0
  N55: Led_HR3_R1.anode, CMOS_AND3.pin10
  N56: Led_HR2_R1.cathode, R_HR2_R2.Pin_0
  N57: Led_HR2_R1.anode, CMOS_AND3.pin6
  N58: Led_HR1_R2.cathode, R_HR1_R2.Pin_0
  N59: Led_HR1_R2.anode, CMOS_AND3.pin9
  N60: CMOS_AND3.pin1, R_in_10.Pin_1
  N61: CMOS_AND3.pin2, R_in_11.Pin_1
  N62: CMOS_AND3.pin3, R_in_12.Pin_1
  N63: CMOS_AND3.pin4, R_in_13.Pin_1
  N64: CMOS_AND3.pin5, R_in_14.Pin_1
  N65: CMOS_AND3.pin8, R_in_18.Pin_0
  N66: CMOS_AND3.pin11, R_in_15.Pin_0
  N67: CMOS_AND3.pin12, R_in_16.Pin_0
  N68: CMOS_AND3.pin13, R_in_17.Pin_0
  N69: Led_HR2_R2.cathode, R_HR2_R3.Pin_0
  N70: Led_HR2_R2.anode, CMOS_AND4.pin6
  N71: Led_HR1_R3.cathode, R_HR1_R3.Pin_0
  N72: Led_HR1_R3.anode, CMOS_AND4.pin9
  N73: CMOS_AND4.pin1, R_in_19.Pin_1
  N74: CMOS_AND4.pin2, R_in_20.Pin_1
  N75: CMOS_AND4.pin3, R_in_21.Pin_1
  N76: CMOS_AND4.pin4, R_in_22.Pin_1
  N77: CMOS_AND4.pin5, R_in_23.Pin_1
  N78: CMOS_AND4.pin8, R_in_27.Pin_0
  N79: CMOS_AND4.pin10, R_in_28.Pin_0
  N80: CMOS_AND4.pin11, R_in_24.Pin_0
  N81: CMOS_AND4.pin12, R_in_25.Pin_0
  N82: CMOS_AND4.pin13, R_in_26.Pin_0
  N83: Led_HR3_R2.cathode, R_HR3_R2.Pin_0
  N84: Led_HR3_R2.anode, CMOS_AND5.pin10
  N85: Led_HR3_R3.cathode, R_HR3_R3.Pin_0
  N86: Led_HR3_R3.anode, CMOS_AND6.pin10
  N87: Led_HR2_R3.cathode, R_HR2_R4.Pin_0
  N88: Led_HR2_R3.anode, CMOS_AND5.pin6
  N89: Led_HR2_R4.cathode, R_HR2_R6.Pin_0
  N90: Led_HR2_R4.anode, CMOS_AND6.pin6
  N91: Led_HR2_R5.cathode, R_HR2_R5.Pin_0
  N92: Led_HR2_R5.anode, CMOS_AND7.pin6
  N93: Led_HR1_R4.cathode, R_HR1_R4.Pin_0
  N94: Led_HR1_R4.anode, CMOS_AND5.pin9
  N95: Led_HR1_R5.cathode, R_HR1_R5.Pin_0
  N96: Led_HR1_R5.anode, CMOS_AND7.pin9
  N97: Led_HR1_R6.cathode, R_HR1_R6.Pin_0
  N98: Led_HR1_R6.anode, CMOS_AND6.pin9
  N99: CMOS_AND5.pin1, R_in_29.Pin_1
  N100: CMOS_AND5.pin2, R_in_32.Pin_1
  N101: CMOS_AND5.pin3, R_in_35.Pin_1
  N102: CMOS_AND5.pin4, R_in_47.Pin_1
  N103: CMOS_AND5.pin5, R_in_46.Pin_1
  N104: CMOS_AND5.pin8, R_in_41.Pin_0
  N105: CMOS_AND5.pin11, R_in_49.Pin_0
  N106: CMOS_AND5.pin12, R_in_48.Pin_0
  N107: CMOS_AND5.pin13, R_in_43.Pin_0
  N108: CMOS_AND6.pin1, R_in_31.Pin_1
  N109: CMOS_AND6.pin2, R_in_34.Pin_1
  N110: CMOS_AND6.pin3, R_in_54.Pin_1
  N111: CMOS_AND6.pin4, R_in_50.Pin_1
  N112: CMOS_AND6.pin5, R_in_36.Pin_1
  N113: CMOS_AND6.pin8, R_in_44.Pin_0
  N114: CMOS_AND6.pin11, R_in_52.Pin_0
  N115: CMOS_AND6.pin12, R_in_53.Pin_0
  N116: CMOS_AND6.pin13, R_in_39.Pin_0
  N117: CMOS_AND7.pin1, R_in_30.Pin_1
  N118: CMOS_AND7.pin2, R_in_33.Pin_1
  N119: CMOS_AND7.pin3, R_in_55.Pin_1
  N120: CMOS_AND7.pin4, R_in_37.Pin_1
  N121: CMOS_AND7.pin5, R_in_42.Pin_1
  N122: CMOS_AND7.pin8, R_in_51.Pin_0
  N123: CMOS_AND7.pin10, R_in_56.Pin_0
  N124: CMOS_AND7.pin11, R_in_45.Pin_0
  N125: CMOS_AND7.pin12, R_in_40.Pin_0
  N126: CMOS_AND7.pin13, R_in_38.Pin_0

notes:
  These LED indicates that player red has gotten three in a row on the horizontal rows
  This section handles
  1) The power for each individual arena LED's
  2) passes the arena's state to the next
  This section handles:
  1) Detection if a player has gotten three in a row
  2) If yes, passes it to the next section
  This LED indicates that player red has three in a row
  This section handles the display of a player having three in a row
  Each connection from below goes to two or three 3AND ports in the section below
  Per player there will be 8 connection from the upper section the the lower section
  1: pin 1 of rotary switch, Red player active
  2: pin 2 of rotary switch, no player active
  3: pin 3 of rotary switch, Green player active
  4: pin A of rotary switch
  These headers are connected to the rotary switches.
  Order:
  top-left, top-mid, top-right,
  mid-left, mid-mid, right-mid,
  bottom-left, bottom-mid, bottom-right
  1) IN 1
  2) IN 1
  3) IN 2
  4) IN 2
  5) IN 2
  6) OUT 2
  7) GND
  8) IN 1
  9) OUT 1
  10) OUT 3
  11) IN 3
  12) IN 3
  13) IN 3
  14) +3 to +15V
  ?CMOS 4075?
  If it is a CMOS 4075:
  1) IN 1
  2) IN 1
  3) IN 2
  4) IN 2
  5) IN 2
  6) OUT 2
  7) GND
  8) IN 1
  9) OUT 1
  10) OUT 3
  11) IN 3
  12) IN 3
  13) IN 3
  14) +3 to +15V
  If it is a CMOS 4072:
  1) OUT 1
  2) IN 1
  3) IN 1
  4) IN 1
  5) IN 1
  6) NC
  7) GND
  8) NC
  9) IN 2
  10) IN 2
  11) IN 2
  12) IN 2
  13) OUT 2
  14) +3 to +15
